# Fritzing sketch pino (saved by Fritzing 0.9.3b)
circuit board: 4.4cm x 4.4cm
circuit board: 5cm x 15.07cm
circuit board: 28cm x 27cm
circuit board: 9.5cm x 7.7cm
circuit board: 4.4cm x 4.4cm
breadboards: 1

parts:
  Atmega_2560 = Arduino Mega ADK (Rev3)
  LM2596 = DIP-Relay-D31A [part_number=D31A*]
  J2 = Screw terminal - 2 pins [package=THT]
  J3 = Screw terminal - 2 pins [package=THT]
  J4 = Screw terminal - 2 pins [package=THT]
  J5 = Screw terminal - 2 pins [package=THT]
  J6 = Screw terminal - 2 pins [package=THT]
  J7 = Screw terminal - 2 pins [package=THT]
  J12 = Screw terminal - 2 pins [package=THT]
  J13 = Screw terminal - 2 pins [package=THT]
  J22 = Screw terminal - 2 pins [package=THT]
  J23 = Screw terminal - 2 pins [package=THT]
  J24 = Screw terminal - 2 pins [package=THT]
  J25 = Screw terminal - 2 pins [package=THT]
  JP2 = Header 3 [package=screwterminal-3.5mm-3_lock.007s]
  JP3 = Header 3 [package=screwterminal-3.5mm-3_lock.007s]
  JP4 = Header 3 [package=screwterminal-3.5mm-3_lock.007s]
  JP5 = Header 3 [package=screwterminal-3.5mm-3_lock.007s]
  JP6 = Header 3 [package=screwterminal-3.5mm-3_lock.007s]
  JP7 = Header 3 [package=screwterminal-3.5mm-3_lock.007s]
  JP8 = Header 3 [package=screwterminal-3.5mm-3_lock.007s]
  JP9 = Header 3 [package=screwterminal-3.5mm-3_lock.007s]
  JP10 = Header 3 [package=screwterminal-3.5mm-3_lock.007s]
  JP11 = Header 3 [package=screwterminal-3.5mm-3_lock.007s]
  JP12 = Header 3 [package=screwterminal-3.5mm-3_lock.007s]
  JP13 = Header 3 [package=screwterminal-3.5mm-3_lock.007s]
  J26 = Screw terminal - 2 pins [package=THT]
  J27 = Screw terminal - 2 pins [package=THT]
  J28 = Screw terminal - 2 pins [package=THT]
  J29 = Screw terminal - 2 pins [package=THT]
  J30 = Screw terminal - 2 pins [package=THT]
  J31 = Screw terminal - 2 pins [package=THT]
  12_VCC = LilyPad Simple Power
  U1 = M10X2 [package=2x10_lock]
  J32 = Power Jack [package=power_jack_smd]
  JP14 = Header 3 [package=screwterminal-3.5mm-3_lock.007s]
  JP15 = Header 3 [package=screwterminal-3.5mm-3_lock.007s]
  JP16 = Header 3 [package=screwterminal-3.5mm-3_lock.007s]
  JP17 = Header 3 [package=screwterminal-3.5mm-3_lock.007s]
  JP18 = Header 3 [package=screwterminal-3.5mm-3_lock.007s]
  JP19 = Header 3 [package=screwterminal-3.5mm-3_lock.007s]
  JP20 = Header 3 [package=screwterminal-3.5mm-3_lock.007s]
  JP21 = Header 3 [package=screwterminal-3.5mm-3_lock.007s]
  Vin_12v_shield = Microphone
  buzzer = Screw terminal - 2 pins [package=THT]
  D31 = Reed switch [package=THT]
  D30 = Reed switch [package=THT]
  D20 = Reed switch [package=THT]
  D29 = Reed switch [package=THT]
  D21 = Reed switch [package=THT]
  D22 = Reed switch [package=THT]
  D23 = Reed switch [package=THT]
  D24 = Reed switch [package=THT]
  D25 = Reed switch [package=THT]
  D28 = Reed switch [package=THT]
  D27 = Reed switch [package=THT]
  D26 = Reed switch [package=THT]
  MOTOR_1 = DC Motor
  MOTOR_2 = DC Motor
  Inclinar_Rampa = Capacitor Polarized [package=panasonic_h13]
  Declinar_Rampa = Capacitor Polarized [package=panasonic_h13]
  Bajar_Rampa = Capacitor Polarized [package=panasonic_h13]
  Subir_Rampa = Capacitor Polarized [package=panasonic_h13]
  Sensor_1 = Resonator [frequency="16 Mhz" package=THT]
  Sensor_2 = Resonator [frequency="16 Mhz" package=THT]
  Sensor_3 = Resonator [frequency="16 Mhz" package=THT]
  Sensor_4 = Resonator [frequency="16 Mhz" package=THT]
  Sensor_5 = Resonator [frequency="16 Mhz" package=THT]
  Sensor_6 = Resonator [frequency="16 Mhz" package=THT]
  JP24 = Header 3 [package=screwterminal-3.5mm-3_lock.007s]  # not connected
  JP25 = Header 3 [package=screwterminal-3.5mm-3_lock.007s]  # not connected
  J33 = Screw terminal - 2 pins [package=THT]  # not connected
  J34 = Screw terminal - 2 pins [package=THT]  # not connected
  J35 = Screw terminal - 2 pins [package=THT]  # not connected
  J36 = Screw terminal - 2 pins [package=THT]  # not connected

nets:
  N1: Atmega_2560.D19/RX1, Sensor_6.0, Sensor_6.1
  N2: Atmega_2560.D18/TX1, Sensor_5.0, Sensor_5.1
  N3: Atmega_2560.D17/RX2, Sensor_4.0, Sensor_4.1
  N4: Atmega_2560.D16/TX2, Sensor_3.0, Sensor_3.1
  N5: Atmega_2560.D15/RX3, Sensor_2.0, Sensor_2.1
  N6: Atmega_2560.D14/TX3, Sensor_1.0, Sensor_1.1
  N7: Atmega_2560.GND, U1.1, U1.2, buzzer.pin1
  N8: Atmega_2560.D12_PWM, buzzer.pin2
  N9: Atmega_2560.D9_PWM, U1.3, U1.4
  N10: Atmega_2560.D8_PWM, U1.5, U1.6
  N11: Atmega_2560.IOREF, Atmega_2560.5V, J12.pin1, J12.pin2, J13.pin1, J13.pin2, JP2.2, JP3.2, JP4.2, JP5.2, JP6.2, JP7.2, JP8.2, JP9.2, JP10.2, JP11.2, JP12.2, JP13.2, J26.pin1, J26.pin2, J27.pin1, J27.pin2, J28.pin1, J28.pin2, J29.pin1, J29.pin2, J30.pin1, J30.pin2, J31.pin1, J31.pin2, U1.19, U1.20
  N12: Atmega_2560.D2_PWM, U1.17, U1.18
  N13: Atmega_2560.D3_PWM, U1.15, U1.16
  N14: Atmega_2560.D4_PWM, U1.13, U1.14
  N15: Atmega_2560.D5_PWM, U1.11, U1.12
  N16: Atmega_2560.D6_PWM, U1.9, U1.10
  N17: Atmega_2560.D7_PWM, U1.7, U1.8
  N18: LM2596.A1_Switch_Terminal_A, LM2596.COIL1_+, J32.PWR
  N19: LM2596.Coil2_-, LM2596.B1_Switch_Terminal_B, LM2596.B2_Switch_Terminal_B, LM2596.Coil_Sheeld, J2.pin1, J2.pin2, J3.pin1, J3.pin2, J4.pin1, J4.pin2, 12_VCC.GND, 12_VCC.+, Vin_12v_shield.pin1
  N20: LM2596.n.c., LM2596.A2_Switch_Terminal_A, J32.GNDBREAK
  N21: J5.pin1, J5.pin2, J6.pin1, J6.pin2, J7.pin1, J7.pin2, Vin_12v_shield.pin2
  N22: J22.pin1, J22.pin2, JP16.1, JP17.1
  N23: J23.pin1, J23.pin2, JP16.3, JP17.3
  N24: J24.pin1, J24.pin2, JP14.1, JP15.1
  N25: J25.pin1, J25.pin2, JP14.3, JP15.3
  N26: JP2.1, D31.pin_1, D31.pin_2
  N27: JP3.1, D30.pin_1, D30.pin_2
  N28: JP4.1, D29.pin_1, D29.pin_2
  N29: JP5.1, D28.pin_1, D28.pin_2
  N30: JP6.1, D27.pin_1, D27.pin_2
  N31: JP7.1, D26.pin_1, D26.pin_2
  N32: JP8.3, D25.pin_1, D25.pin_2
  N33: JP9.3, D20.pin_1, D20.pin_2
  N34: JP10.3, D22.pin_1, D22.pin_2
  N35: JP11.3, D21.pin_1, D21.pin_2
  N36: JP12.3, D24.pin_1, D24.pin_2
  N37: JP13.3, D23.pin_1, D23.pin_2
  N38: JP14.2, MOTOR_1.pin_1
  N39: JP15.2, MOTOR_1.pin_2
  N40: JP16.2, MOTOR_2.pin_2
  N41: JP17.2, MOTOR_2.pin_1
  N42: JP18.1, Inclinar_Rampa.+
  N43: JP18.2, Inclinar_Rampa.-
  N44: JP19.1, Bajar_Rampa.+
  N45: JP19.2, Bajar_Rampa.-
  N46: JP20.1, Declinar_Rampa.+
  N47: JP20.2, Declinar_Rampa.-
  N48: JP21.1, Subir_Rampa.+
  N49: JP21.2, Subir_Rampa.-

notes:
  +VCC12v
  GND
  +VCC9v
  OUT
  INN
  5v arduino
